// Logisim project Banco de regs.circ as structural Verilog
module Registrador (
  input  in_1,
  input  [7:0] VALOR,
  output [7:0] \SAÍDA 
);

  D_Flip_Flop d_ff_1 (.clk(in_1), .D(VALOR[7]), .Q(\SAÍDA [7]));  // open: Qn, preset, en, reset
  D_Flip_Flop d_ff_2 (.clk(in_1), .D(VALOR[6]), .Q(\SAÍDA [6]));  // open: Qn, preset, en, reset
  D_Flip_Flop d_ff_3 (.clk(in_1), .D(VALOR[5]), .Q(\SAÍDA [5]));  // open: Qn, preset, en, reset
  D_Flip_Flop d_ff_4 (.clk(in_1), .D(VALOR[4]), .Q(\SAÍDA [4]));  // open: Qn, preset, en, reset
  D_Flip_Flop d_ff_5 (.clk(in_1), .D(VALOR[3]), .Q(\SAÍDA [3]));  // open: Qn, preset, en, reset
  D_Flip_Flop d_ff_6 (.clk(in_1), .D(VALOR[2]), .Q(\SAÍDA [2]));  // open: Qn, preset, en, reset
  D_Flip_Flop d_ff_7 (.clk(in_1), .D(VALOR[1]), .Q(\SAÍDA [1]));  // open: Qn, preset, en, reset
  D_Flip_Flop d_ff_8 (.clk(in_1), .D(VALOR[0]), .Q(\SAÍDA [0]));  // open: Qn, preset, en, reset
endmodule

module Banco_de_registradores (
  input  [7:0] VALOR,
  input  [1:0] \ENDEREÇO ,
  input  [1:0] \ENDEREÇO_2 ,
  output [7:0] out_4,
  output [7:0] out_5
);

  wire and_1_out, and_2_out, and_3_out, and_4_out, and_5_out, and_6_out, and_7_out, and_8_out, and_9_out,
       and_10_out, and_11_out, and_12_out, and_13_out, and_14_out, and_15_out, and_16_out, clock_1_out,
       not_1_out, not_2_out, not_3_out, not_4_out, not_5_out, not_6_out, not_7_out, not_8_out;
  wire [7:0] \registrador_1_saída , \registrador_2_saída , \registrador_3_saída , \registrador_4_saída ,
       \registrador_5_saída , \registrador_6_saída , \registrador_7_saída , \registrador_8_saída ;

  not not_1 (not_1_out, \ENDEREÇO [1]);
  not not_2 (not_2_out, \ENDEREÇO [0]);
  not not_3 (not_3_out, \ENDEREÇO [0]);
  not not_4 (not_4_out, \ENDEREÇO [1]);
  not not_5 (not_5_out, \ENDEREÇO_2 [1]);
  not not_6 (not_6_out, \ENDEREÇO_2 [0]);
  not not_7 (not_7_out, \ENDEREÇO_2 [0]);
  not not_8 (not_8_out, \ENDEREÇO_2 [1]);
  Clock clock_1 (.out(clock_1_out));
  and and_1 (and_1_out, not_1_out, not_2_out);
  and and_2 (and_2_out, \ENDEREÇO [1], not_3_out, not_3_out);
  and and_3 (and_3_out, not_4_out, \ENDEREÇO [0]);
  and and_4 (and_4_out, \ENDEREÇO [1], \ENDEREÇO [0]);
  and and_5 (and_5_out, not_5_out, not_6_out);
  and and_6 (and_6_out, \ENDEREÇO_2 [1], not_7_out, not_7_out);
  and and_7 (and_7_out, not_8_out, \ENDEREÇO_2 [0]);
  and and_8 (and_8_out, \ENDEREÇO_2 [1], \ENDEREÇO_2 [0]);
  and and_9 (and_9_out, clock_1_out, and_1_out);
  and and_10 (and_10_out, clock_1_out, and_2_out);
  and and_11 (and_11_out, clock_1_out, and_3_out);
  and and_12 (and_12_out, and_4_out, clock_1_out);
  and and_13 (and_13_out, clock_1_out, and_5_out);
  and and_14 (and_14_out, clock_1_out, and_6_out);
  and and_15 (and_15_out, clock_1_out, and_7_out);
  and and_16 (and_16_out, and_8_out, clock_1_out);
  Registrador registrador_1 (.VALOR(VALOR), .\SAÍDA (\registrador_1_saída ), .in_1(and_9_out));
  Registrador registrador_2 (.VALOR(VALOR), .\SAÍDA (\registrador_2_saída ), .in_1(and_10_out));
  Registrador registrador_3 (.VALOR(VALOR), .\SAÍDA (\registrador_3_saída ), .in_1(and_11_out));
  Registrador registrador_4 (.VALOR(VALOR), .\SAÍDA (\registrador_4_saída ), .in_1(and_12_out));
  Registrador registrador_5 (.VALOR(VALOR), .\SAÍDA (\registrador_5_saída ), .in_1(and_13_out));
  Registrador registrador_6 (.VALOR(VALOR), .\SAÍDA (\registrador_6_saída ), .in_1(and_14_out));
  Registrador registrador_7 (.VALOR(VALOR), .\SAÍDA (\registrador_7_saída ), .in_1(and_15_out));
  Registrador registrador_8 (.VALOR(VALOR), .\SAÍDA (\registrador_8_saída ), .in_1(and_16_out));
  Multiplexer #(.select(2), .width(8)) multiplexer_1 (
    .in0(\registrador_5_saída ), .in1(\registrador_6_saída ), .in2(\registrador_7_saída ),
    .in3(\registrador_8_saída ), .out(out_5), .sel(\ENDEREÇO_2 ));  // open: en
  Multiplexer #(.select(2), .width(8)) multiplexer_2 (
    .in0(\registrador_1_saída ), .in1(\registrador_2_saída ), .in2(\registrador_3_saída ),
    .in3(\registrador_4_saída ), .out(out_4), .sel(\ENDEREÇO ));  // open: en
endmodule
