// Logisim project Extensor de sinal.circ as structural Verilog: 1 circuit, main circuit EXTENSOR DE SINAL
module EXTENSOR_DE_SINAL (
  input  [3:0] ENTRADA,
  output [7:0] \SAÍDA 
);


  assign \SAÍDA  = {4'b0000, ENTRADA};
endmodule
