// Logisim project FLIPFLOP D.circ as structural Verilog: 1 circuit, main circuit main
module main (
  input  D,
  input  SET,
  input  CLEAR,
  input  SET_2,
  input  D_2,
  input  CLEAR_2,
  output \SAÍDA ,
  output Q,
  output nQ
);

  wire clock_1_out, clock_2_out, nand_1_out, nand_2_out, nand_3_out, nand_4_out, nand_5_out, nand_6_out,
       not_1_out, not_2_out;

  Clock clock_1 (.out(clock_1_out));
  Clock clock_2 (.out(clock_2_out));
  not not_1 (not_1_out, D_2);
  D_Flip_Flop d_ff_1 (.clk(clock_1_out), .D(D), .Q(\SAÍDA ), .preset(SET), .reset(CLEAR));  // open: Qn, en
  not not_2 (not_2_out, clock_2_out);
  nand nand_1 (nand_1_out, nQ, D_2, clock_2_out);
  nand nand_2 (nand_2_out, clock_2_out, not_1_out, Q);
  nand nand_3 (nand_3_out, SET_2, nand_1_out, nand_1_out, nand_4_out);
  nand nand_4 (nand_4_out, nand_3_out, nand_2_out, CLEAR_2);
  nand nand_5 (nand_5_out, CLEAR_2, nand_3_out, not_2_out);
  nand nand_6 (nand_6_out, not_2_out, nand_4_out, SET_2);
  nand nand_7 (Q, SET_2, nand_5_out, nQ);
  nand nand_8 (nQ, Q, nand_6_out, CLEAR_2);
endmodule
