// Logisim project FLIPFLOP JK.circ as structural Verilog: 1 circuit, main circuit main
module main (
  input  J,
  input  K,
  input  SET,
  input  CLEAR,
  input  SET_2,
  input  J_2,
  input  Q,
  input  CLEAR_2,
  output \SAÍDA ,
  output Q_2,
  output nQ
);

  wire clock_2_out, CLOCK_out, nand_1_out, nand_2_out, nand_3_out, nand_4_out, nand_5_out, nand_6_out,
       not_1_out;

  Clock CLOCK (.out(CLOCK_out));
  J_K_Flip_Flop j_k_ff_1 (.J(J), .clk(CLOCK_out), .K(K), .Q(\SAÍDA ), .preset(SET), .reset(CLEAR));  // open: Qn, en
  Clock clock_2 (.out(clock_2_out));
  not not_1 (not_1_out, clock_2_out);
  nand nand_1 (nand_1_out, nQ, J_2, clock_2_out);
  nand nand_2 (nand_2_out, clock_2_out, Q, Q_2);
  nand nand_3 (nand_3_out, SET_2, nand_1_out, nand_1_out, nand_4_out);
  nand nand_4 (nand_4_out, nand_3_out, nand_2_out, CLEAR_2);
  nand nand_5 (nand_5_out, CLEAR_2, nand_3_out, not_1_out);
  nand nand_6 (nand_6_out, not_1_out, nand_4_out, SET_2);
  nand nand_7 (Q_2, SET_2, nand_5_out, nQ);
  nand nand_8 (nQ, Q_2, nand_6_out, CLEAR_2);
endmodule
