// Logisim project MULTIPLEXADOR, 4.circ as structural Verilog: 1 circuit, main circuit main
module main (
  input  A,
  input  B,
  input  C,
  input  D,
  input  \ENDEREÇO_01 ,
  input  \ENDEREÇO_02 ,
  output \SAÍDA 
);

  wire and_1_out, and_2_out, and_3_out, and_4_out, not_1_out, not_2_out;

  not not_1 (not_1_out, \ENDEREÇO_01 );
  not not_2 (not_2_out, \ENDEREÇO_02 );
  and and_1 (and_1_out, A, \ENDEREÇO_02 , \ENDEREÇO_01 );
  and and_2 (and_2_out, B, not_1_out, \ENDEREÇO_02 );
  and and_3 (and_3_out, not_2_out, C, \ENDEREÇO_01 );
  and and_4 (and_4_out, D, not_1_out, not_2_out);
  or or_1 (\SAÍDA , and_1_out, and_2_out, and_3_out, and_4_out);
endmodule
