// Logisim project MemoriaRAM.circ as structural Verilog: 1 circuit, main circuit main
module main (
  input  in_1,
  input  in_2,
  input  in_3,
  input  in_4,
  input  in_5,
  input  in_6,
  input  in_7,
  input  in_8,
  input  in_9,
  input  in_10,
  input  in_11,
  input  in_12,
  input  in_13,
  input  in_14,
  input  in_15,
  input  in_16,
  input  in_17,
  input  in_18,
  input  in_19,
  input  in_20,
  input  in_21,
  output [7:0] out_22
);

  wire clock_1_out;
  wire [7:0] controlled_buffer_2_out;

  assign out_22 = in_9 ? {in_1, in_2, in_3, in_4, in_5, in_6, in_7, in_8} : 8'bz;  // Controlled_Buffer controlled_buffer_1
  Clock clock_1 (.out(clock_1_out));
  assign controlled_buffer_2_out = in_19 ? out_22 : 8'bz;  // Controlled_Buffer controlled_buffer_2
  assign out_22 = in_21 ? controlled_buffer_2_out : 8'bz;  // Controlled_Buffer controlled_buffer_3
  RAM ram_1 (
    .addr({in_10, in_11, in_12, in_13, in_14, in_15, in_16, in_17}), .data(controlled_buffer_2_out),
    .clk(clock_1_out), .ld(in_20), .clr(in_18));  // open: sel

  // Notes on the sheet:
  //   Endereço que irá ser execultado
  //   e armazenado na memória
  //   Barramento
  //   Memória RAM de 8 bits
  //   Memória RAM
  //   Envia dados do Barramento para a Memória, assim como da Memória para o Barramento
  //   Endereço de memória
endmodule
