// Logisim project MemoriaROM.circ as structural Verilog: 1 circuit, main circuit main
module main (
  input  [7:0] Entrada_de_Bits
);

  wire undriven;
  wire [7:0] rom_1_data;

  ROM rom_1 (.addr(Entrada_de_Bits), .data(rom_1_data), .sel(undriven));
  Hex_Digit_Display hex_digit_display_1 (.value(rom_1_data[7:4]));  // open: dp
  Hex_Digit_Display hex_digit_display_2 (.value(rom_1_data[3:0]));  // open: dp

  // Notes on the sheet:
  //   Memória ROM de 8 bits
  //   contents of rom_1 (hex, n*v repeats v):
  //   1 2 3 4 5 12 20 23 42 55 74 81 85 89 92 98 34 67 97 23 45 76 26 56 34 58 22 17 29 13 4 11
endmodule
