// Logisim project Somador.circ as structural Verilog: 4 circuits, main circuit Somador
module Somador (
  input  CIN,
  input  A,
  input  B,
  output S,
  output COUT
);

  wire and_1_out, and_2_out, xor_1_out;

  xor xor_1 (xor_1_out, A, B);
  and and_1 (and_1_out, A, B);
  xor xor_2 (S, CIN, xor_1_out);
  and and_2 (and_2_out, CIN, xor_1_out);
  or or_1 (COUT, and_2_out, and_1_out);
endmodule

// sum 4-bit
module ADD (
  input  CIN,
  input  A0,
  input  B0,
  input  A1,
  input  B1,
  input  A2,
  input  B2,
  input  A3,
  input  B3,
  output S1,
  output S2,
  output S3,
  output S4,
  output COUT
);

  wire somador_2_cout, somador_3_cout, somador_cout;

  Somador somador (.CIN(CIN), .A(A0), .B(B0), .S(S1), .COUT(somador_cout));
  Somador somador_2 (.CIN(somador_cout), .A(A1), .B(B1), .S(S2), .COUT(somador_2_cout));
  Somador somador_3 (.CIN(somador_2_cout), .A(A2), .B(B2), .S(S3), .COUT(somador_3_cout));
  Somador somador_4 (.CIN(somador_3_cout), .A(A3), .B(B3), .S(S4), .COUT(COUT));
endmodule

module somador_8_bit (
  input  CIN,
  input  A0,
  input  BO,
  input  A1,
  input  B1,
  input  A2,
  input  B2,
  input  A3,
  input  B3,
  input  A4,
  input  B4,
  input  A5,
  input  B5,
  input  A6,
  input  A7,
  input  B7,
  output COUT
);

  wire add_1_cout;
  wire [3:0] add_1_s1, add_2_s1;

  ADD add_1 (
    .CIN(CIN), .A0(A0), .B0(BO), .A1(A1), .B1(B1), .A2(A2), .B2(B2), .A3(A3), .B3(B3), .S1(add_1_s1[0]),
    .S2(add_1_s1[1]), .S3(add_1_s1[2]), .S4(add_1_s1[3]), .COUT(add_1_cout));
  ADD add_2 (
    .CIN(add_1_cout), .A0(A4), .B0(B4), .A1(A5), .B1(B5), .A2(A6), .B2(1'b1), .A3(A7), .B3(B7),
    .S1(add_2_s1[0]), .S2(add_2_s1[1]), .S3(add_2_s1[2]), .S4(add_2_s1[3]), .COUT(COUT));
  Hex_Digit_Display hex_digit_display_1 (.value(add_2_s1));  // open: dp
  Hex_Digit_Display hex_digit_display_2 (.value(add_1_s1));  // open: dp
endmodule

module SOMADOR (
  input  _01,
  input  _02,
  input  in_3,
  input  _03,
  input  _04,
  input  _05,
  input  _06,
  input  _07,
  input  _08,
  output [7:0] \SAÍDA ,
  output OVERFLOW
);

  wire adder_1_cout, adder_2_cout, adder_3_cout, adder_4_cout, adder_5_cout, adder_6_cout, adder_7_cout;

  Adder #(.width(1)) adder_1 (.a(_01), .b(1'b0), .out(\SAÍDA [0]), .cin(in_3), .cout(adder_1_cout));
  Adder #(.width(1)) adder_2 (.a(_02), .b(1'b0), .out(\SAÍDA [1]), .cin(adder_1_cout), .cout(adder_2_cout));
  Adder #(.width(1)) adder_3 (.a(_03), .b(1'b1), .out(\SAÍDA [2]), .cin(adder_2_cout), .cout(adder_3_cout));
  Adder #(.width(1)) adder_4 (.a(_04), .b(1'b0), .out(\SAÍDA [3]), .cin(adder_3_cout), .cout(adder_4_cout));
  Adder #(.width(1)) adder_5 (.a(_05), .b(1'b0), .out(\SAÍDA [4]), .cin(adder_4_cout), .cout(adder_5_cout));
  Adder #(.width(1)) adder_6 (.a(_06), .b(1'b0), .out(\SAÍDA [5]), .cin(adder_5_cout), .cout(adder_6_cout));
  Adder #(.width(1)) adder_7 (.a(_07), .b(1'b0), .out(\SAÍDA [6]), .cin(adder_6_cout), .cout(adder_7_cout));
  Adder #(.width(1)) adder_8 (.a(_08), .b(1'b0), .out(\SAÍDA [7]), .cin(adder_7_cout), .cout(OVERFLOW));
endmodule
