// Logisim project ULA.circ as structural Verilog: 1 circuit, main circuit ULA
module ULA (
  input  [7:0] A,
  input  [7:0] B,
  input  [3:0] in_3,
  input  [2:0] in_4,
  output [7:0] \SAÍDA 
);

  wire [7:0] adder_1_out, and_1_out, nand_1_out, nor_1_out, not_1_out, or_1_out, shifter_1_out,
       shifter_2_out, subtractor_1_out, xor_1_out;

  Adder adder_1 (.a(A), .b(B), .out(adder_1_out));  // open: cin, cout
  Subtractor subtractor_1 (.a(A), .b(B), .out(subtractor_1_out));  // open: bin, bout
  Shifter shifter_1 (.in(A), .\dist (in_4), .out(shifter_1_out));
  Shifter #(.shift("lr")) shifter_2 (.in(A), .\dist (in_4), .out(shifter_2_out));
  assign not_1_out = ~A;  // NOT_Gate not_1, 8 bits wide
  assign nand_1_out = ~(A & B);  // NAND_Gate nand_1, 8 bits wide
  assign and_1_out = A & B;  // AND_Gate and_1, 8 bits wide
  assign nor_1_out = ~(A | B);  // NOR_Gate nor_1, 8 bits wide
  assign xor_1_out = A ^ B;  // XOR_Gate xor_1, 8 bits wide
  assign or_1_out = A | B;  // OR_Gate or_1, 8 bits wide
  Multiplexer #(.select(4), .width(8)) multiplexer_1 (
    .in0(nand_1_out), .in1(and_1_out), .in2(nor_1_out), .in3(xor_1_out), .in4(or_1_out), .in5(adder_1_out),
    .in6(subtractor_1_out), .in7(shifter_1_out), .in8(shifter_2_out), .in9(not_1_out), .out(\SAÍDA ),
    .sel(in_3));  // open: in10, in11, in12, in13, in14, in15, en

  // Notes on the sheet:
  //   ULA de 8 bits, utilizando port map, com as seguintes operações: AND, OR, NOT, NOR, NAND, XOR, SHIFT de 2 bits à esquerda, SHIFT de bits à direita, soma e subtração.
  //   0000 - NAND
  //   0001 - AND
  //   0010 - NOR
  //   0011- XOR
  //   0100 - OR
  //   0101 - SOMA
  //   0110 - SUBTRAÇÃO
  //   1001 - NOT
  //   0111 - SHIFT P/ ESQUERDA
  //   1000 - SHIFT P/ DIREITA
endmodule
