// Logisim project Unidade de controle.circ as structural Verilog: 1 circuit, main circuit Unidade de controle
module Unidade_de_controle (
  input  [2:0] in_1,
  output JUMP,
  output OP01,
  output OP02,
  output BRANCH,
  output MEMWRITE,
  output MEMREAD,
  output REGWRITE,
  output MEMREG,
  output SRC,
  output REGDEST
);

  Multiplexer #(.select(3), .width(10)) multiplexer_1 (
    .in0(10'h144), .in1(10'h2c1), .in2(10'h1), .in3(10'ha), .in4(10'h146), .in5(10'h116), .in6(10'h1e6),
    .in7(10'h240), .out({REGDEST, SRC, MEMREG, REGWRITE, MEMREAD, MEMWRITE, BRANCH, OP02, OP01, JUMP}),
    .sel(in_1));  // open: en

  // Notes on the sheet:
  //   sinais de controle
  //   000 - R-TYPE
  //   001 - LW
  //   010 - SW
  //   011 - ADD
  //   100 - BEQ
  //   101 - J
  //   110 - JAL
  //   111 - SALTO INCONDICIONAL
endmodule
